# Fritzing sketch 74hc595 (saved by Fritzing 0.9.3b)
breadboards: 1

parts:
  WeMos_D1_Mini1 = WeMos D1 Mini
  IC1 = SHIFT REGISTER [package=dil16]
  IC2 = ULN2003A [package="DIP16 [THT]"]

nets:
  N1: WeMos_D1_Mini1.G, IC1.GND, IC1.G, IC2.0V
  N2: IC1.QB, IC2.In_1
  N3: IC1.QC, IC2.In_2
  N4: IC1.QD, IC2.In_3
  N5: IC1.QE, IC2.In_4
  N6: IC1.QF, IC2.In_5
  N7: IC1.QG, IC2.In_6
  N8: IC1.QH, IC2.In_7
  N9: IC1.SCL, IC1.VCC

notes:
  7 outputs
  common input Vdd
