# Fritzing sketch airqual (saved by Fritzing 0.9.3b)
breadboards: 1

parts:
  WeMos_D1_Mini1 = WeMos D1 Mini
  R2 = Resistor [tolerance=±5% resistance=10k package="2512 [SMD]"]
  Bauteil1 = Adafruit CCS811
  DHT1 = DHT22 Humidity and Temperature Sensor
  Bauteil2 = Adafruit BMP085 [part_number="Adafruit #391"]

nets:
  3V3: WeMos_D1_Mini1.3V3, R2.Pin_1, Bauteil1.VIN, DHT1.VDD
  N1: WeMos_D1_Mini1.G, Bauteil1.GND, Bauteil1.!WAKE
  N2: R2.Pin_0, DHT1.DATA
  GND: DHT1.GND, Bauteil2.GND

custom parts:
  Adafruit BMP085: This precision sensor from Bosch is the best low-cost sensing solution for measuring barometric pressure and temperature. Because pressure changes with altitude you can also use it as an altimeter! The sensor is soldered onto a PCB with a 3.3V regulator, I2C level shifter and pull-up resistors on the I2C pins. NEW! We now have a fully 5V compliant version of this board - a 3.3V regulator and a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
