# Fritzing sketch light (saved by Fritzing 0.9.3b)
breadboards: 1

parts:
  WeMos_D1_Mini1 = WeMos D1 Mini
  R1 = Photocell (LDR) [package=THT]
  R2 = Resistor [tolerance=±5% resistance=10k package="2512 [SMD]"]
  Bauteil1 = Adafruit TSL2561 [part_number="Adafruit #439"]

nets:
  3V3: WeMos_D1_Mini1.3V3, R1.pin_0, Bauteil1.VIN
  N1: WeMos_D1_Mini1.G, R2.Pin_0, Bauteil1.GND
  N2: R1.pin_1, R2.Pin_1

custom parts:
  Adafruit TSL2561: The TSL2561 luminosity sensor is an advanced digital light sensor, ideal for use in a wide range of light situations. Compared to low cost CdS cells, this sensor is more precise, allowing for exact lux calculations and can be configured for different gain/timing ranges to detect light ranges from up to 0.1 - 40,000+ Lux on the fly. The best part of this sensor is that it contains both infrared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
