# Fritzing sketch servo (saved by Fritzing 0.9.3b)
breadboards: 1

parts:
  WeMos_D1_Mini1 = WeMos D1 Mini
  Bauteil1 = 16-Channel 12-bit PWM Servo Driver - I2C [part_number=815]
  J1 = Basic Servo

nets:
  N1: WeMos_D1_Mini1.D1, Bauteil1.SCL
  N2: WeMos_D1_Mini1.D2, Bauteil1.SDA
  VCC: Bauteil1.5.0V, Bauteil1.VCC, J1.vcc
  GND: Bauteil1.OE, Bauteil1.GND, J1.gnd
  N3: Bauteil1.PWM15, J1.pulse

notes:
  5V (extern) for servos

custom parts:
  16-Channel 12-bit PWM Servo Driver - I2C: You want to make a cool robot, maybe a hexapod walker, or maybe just a piece of art with a lot of moving parts. Or maybe you want to drive a lot of LEDs with precise PWM output. Using only two pins, control 16 free-running PWM outputs! You can even chain up 62 breakouts to control up to 992 PWM outputs.
